# Fritzing sketch sgDevice2 (saved by Fritzing 0.9.3b)
circuit board: 10cm x 6cm
breadboards: 1

parts:
  J1 = shrouded pin header, 6 pins [form="♂ (shrouded male)"]
  IC2 = IC, DIP package, 8 pins [chip_label=6N137]
  R4 = Resistor [tolerance=±5% resistance=10k package=THT]
  D2 = Diode [package=diode-1n4148]
  R5 = Resistor [tolerance=±5% resistance=220 package=THT]
  R6 = Resistor [tolerance=±1% resistance=10k package=THT]
  J1' = double row female pin header, 6 pins [form="♀ (female)"]
  J2' = double row female pin header, 20 pins [form="♀ (female)"]
  Poti1 = POT [package=pot_mammoth]
  Jack1 = AUDIO-JACK2 [package=audio-jack]
  Jack2 = AUDIO-JACK2 [package=audio-jack]
  Poti2 = POT [package=pot_mammoth]
  Bauteil2 = Arduino Mega Proto Shield (v6)
  J3 = double row female pin header, 32 pins [form="♀ (female)"]
  J3' = double row male pin header, 32 pins [form="♂ (male)"]
  Switch1 = Toggle Switch [package=THT]
  J2 = shrouded pin header, 20 pins [form="♂ (shrouded male)"]
  S4 = Toggle Switch [package=THT]
  Trigger1 = Momentary Switch [package=ksa_sealed_tac_switch]
  MIDI_In = DIN-5 jack (MIDI) [package=THT]
  MIDI_Out = DIN-5 jack (MIDI) [package=THT]

nets:
  MIDI-In Pin 4: J1.pin1, R5.Pin_0, Bauteil2.N$83
  MIDI-In Pin 5: J1.pin2, IC2.pin3, D2.A, Bauteil2.N$71, Bauteil2.N$72
  N1: J1.pin3, Bauteil2.N$59
  N2: J1.pin4, Bauteil2.N$58
  N3: J1.pin5, R6.Pin_1, Bauteil2.N$70, Bauteil2.N$259
  N4: J1.pin6, Bauteil2.TX1, Bauteil2.N$82
  N5: IC2.pin1, Bauteil2.N$48
  N6: IC2.pin2, D2.C, R5.Pin_1, Bauteil2.N$49, Bauteil2.N$62
  N7: IC2.pin4, Bauteil2.N$86
  GND: IC2.pin5, Bauteil2.GND, Bauteil2.N$84, Bauteil2.N$370, J2.pin20
  N8: IC2.pin6, R4.Pin_1, Bauteil2.RX1, Bauteil2.N$65#278, Bauteil2.N$79
  N9: IC2.pin7, Bauteil2.N$65#277
  5V: IC2.pin8, R4.Pin_0, R6.Pin_0, Bauteil2.+5V, Bauteil2.N$55, Bauteil2.N$285, Bauteil2.N$366, J2.pin1
  N10: J1'.pin1, MIDI_In.4
  N11: J1'.pin2, MIDI_In.5
  N12: J1'.pin6, MIDI_Out.GND
  N13: J2'.pin1, Jack1.TIP, Jack2.TIP
  N14: J2'.pin2, Jack1.RING
  N15: J2'.pin3, Jack2.RING
  N16: J2'.pin20, Poti1.A, Jack1.SLEEVE, Jack2.SLEEVE, Poti2.A, Switch1.COM, S4.COM, Trigger1.1
  N17: Poti1.S, Jack1.RSH
  N18: Poti1.E, Jack1.TSH
  N19: Jack2.RSH, Poti2.S
  N20: Jack2.TSH, Poti2.E
  N21: Bauteil2.A9, Bauteil2.N$445, J2.pin11
  N22: Bauteil2.A11, Bauteil2.N$443, J2.pin13
  N23: Bauteil2.A12, Bauteil2.N$442, J2.pin14
  N24: Bauteil2.A14, J2.pin16
  N25: Bauteil2.A1, Bauteil2.N$326, J2.pin3
  N26: Bauteil2.A2, Bauteil2.N$325, J2.pin4
  N27: Bauteil2.A3, J2.pin5
  N28: Bauteil2.A5, Bauteil2.N$450, J2.pin7
  N29: Bauteil2.A6, Bauteil2.N$454, J2.pin8
  N30: Bauteil2.A7, Bauteil2.N$455, J2.pin9
  N31: Bauteil2.A8, Bauteil2.N$456, J2.pin10
  N32: Bauteil2.A10, Bauteil2.N$444, J2.pin12
  N33: Bauteil2.A13, Bauteil2.N$441, J2.pin15
  N34: Bauteil2.A15, Bauteil2.N$324, J2.pin17
  N35: Bauteil2.A0, Bauteil2.N$327, J2.pin2
  N36: Bauteil2.A4, Bauteil2.N$449, J2.pin6
  N37: Bauteil2.D22, J3.pin1
  N38: Bauteil2.N$368, J2.pin18
  N39: Bauteil2.N$369, J2.pin19
  N40: J3'.pin1, Trigger1.3
  N41: J3'.pin9, Switch1.L2
  N42: J3'.pin17, S4.L2

notes:
  MIDI IO
  pins numbered from BACKSIDE!!
  NOTE:
  The "J1..." represent Pin header connections. Pin numbering might be different in the hardware...
  Planned:
  Trigger1.. Trigger8,
  Switch1..Switch8
  Switch9..Switch16
  Footswitch1..Footswitch?
  Planned:
  Poti1..Poti16,
  Jack1..Jack16 (maybe less)
  Every Poti (maybe most) can be replaced by plugging a footpedal
  ... x16
  ...x8
  TODO
  sgDevice2, second version for my MIDI device
